// Logisim project Circuito Guess The Number Xtreme.circ as structural Verilog: 18 circuits, main circuit main
module main (
  input  in_1,
  input  in_2,
  input  in_3,
  input  in_4,
  input  in_5,
  input  in_6,
  input  in_7,
  input  in_8
);

  wire _0, _0A, _0B, _1, _2, _3, _4, _5, A_JOGANDO, A_VENCEU, ACERTOU, and_1_out, and_10_out, AWIN,
       B_JOGANDO, B_VENCEU, BWIN, CHUTANDO_X, CHUTANDO_Y, CHUTAR, clock_1_out, comparador_simples_2_igual,
       comparador_simples_3_igual, CONFIGURAR, DMA, DMB, DSA, DSB, EMPATE, FIM_DE_JOGO, IGUAL, jogo_2_1_clk,
       MAIOR, MENOR, on, or_1_out, or_3_out, or_4_out, or_5_out, or_6_out, or_7_out, or_8_out, plus_1A,
       plus_1B, PodeX, PodeY, \PRÓXIMO , RES, RESETAR, START, SX, SY, T, tunnel, UMA, UMB, USA, USB;
  wire [2:0] S;
  wire [3:0] C, dma_t, dmb_t, dsa_t, dsb_t, GA, GB, GX, GY, PA, PB, sct1, sct2, uma_t, umb_t, usa_t, usb_t,
       x, y;

  Button button_1 (.out(UMA));
  Button button_2 (.out(DMA));
  Hex_Digit_Display hex_digit_display_1 (.value(uma_t));  // open: dp
  Hex_Digit_Display hex_digit_display_2 (.value(dma_t));  // open: dp
  nand nand_1 (T, on, or_1_out);
  and and_1 (and_1_out, _0A, on, _0B);
  Hex_Digit_Display hex_digit_display_3 (.value(PA));  // open: dp
  LED led_1 (.in(1'b1));
  LED led_2 (.in(1'b1));
  LED led_3 (.in(in_1));
  Hex_Digit_Display hex_digit_display_4 (.value(GA));  // open: dp
  LED led_4 (.in(A_JOGANDO));
  Placar placar_1 (.AUMENTAR(plus_1A), .CLEAR(RESETAR), .Display(PA), .Venceu(AWIN));
  and and_2 (A_JOGANDO, or_1_out, on);
  or or_1 (or_1_out, _0, _1, _2);
  or or_2 (FIM_DE_JOGO, and_1_out, or_3_out);
  or or_3 (or_3_out, AWIN, BWIN);
  comparador_simples comparador_simples_1 (
    .in_1(PA), .in_2(PB), .FIM_DE_JOGO(FIM_DE_JOGO), .Menor(A_VENCEU), .Igual(EMPATE), .Maior(B_VENCEU));
  Button button_3 (.out(DSA));
  Button button_4 (.out(USA));
  Hex_Digit_Display hex_digit_display_5 (.value(usa_t));  // open: dp
  Hex_Digit_Display hex_digit_display_6 (.value(dsa_t));  // open: dp
  Placar placar_2 (.AUMENTAR(plus_1B), .CLEAR(RESETAR), .Display(PB), .Venceu(BWIN));
  and and_3 (B_JOGANDO, ~or_1_out, on);  // AND_Gate
  and and_4 (PodeX, or_4_out, on);
  or or_4 (or_4_out, _0, _3);
  and and_5 (PodeY, or_5_out, on);
  or or_5 (or_5_out, _1, _4);
  and and_6 (ACERTOU, comparador_simples_2_igual, RES, comparador_simples_3_igual);
  comparador_simples comparador_simples_2 (
    .in_1(x), .in_2(sct1), .FIM_DE_JOGO(1'b1), .Igual(comparador_simples_2_igual));  // open: Menor, Maior
  comparador_simples comparador_simples_3 (
    .in_1(y), .in_2(sct2), .FIM_DE_JOGO(1'b1), .Igual(comparador_simples_3_igual));  // open: Menor, Maior
  LED led_5 (.in(A_VENCEU));
  Button button_5 (.out(RESETAR));
  LED led_6 (.in(MENOR));
  LED led_7 (.in(SX));
  LED led_8 (.in(FIM_DE_JOGO));
  LED led_9 (.in(EMPATE));
  LED led_10 (.in(tunnel));
  Button button_6 (.out(CONFIGURAR));
  LED led_11 (.in(ACERTOU));
  LED led_12 (.in(IGUAL));
  Button button_7 (.out(CHUTAR));
  Hex_Digit_Display hex_digit_display_7 (.value(GX));  // open: dp
  LED led_13 (.in(CHUTANDO_X));
  Chute chute_1 (
    .CLK(CHUTAR), .\PRÓXIMO (\PRÓXIMO ), .Led(CHUTANDO_X), .Display(x), .CLEAR(RESETAR), .X_Y(C), .Estado(S),
    .CHUTANDO(PodeX), .Sinal(SX));
  Chute chute_2 (
    .CLK(CHUTAR), .\PRÓXIMO (\PRÓXIMO ), .Led(CHUTANDO_Y), .Display(y), .CLEAR(RESETAR), .X_Y(C), .Estado(S),
    .CHUTANDO(PodeY), .Sinal(SY));
  and and_7 (plus_1A, ACERTOU, _2);
  and and_8 (plus_1B, ACERTOU, _5);
  Button button_8 (.out(\PRÓXIMO ));
  LED led_14 (.in(SY));
  Hex_Digit_Display hex_digit_display_8 (.value(GY));  // open: dp
  LED led_15 (.in(CHUTANDO_Y));
  LED led_16 (.in(B_VENCEU));
  Button button_9 (.out(START));
  LED led_17 (.in(MAIOR));
  \Módulo  \módulo_1  (.\NÚMERO ({in_1, in_2, in_3, in_4}), .\Módulo (GA));
  \Módulo  \módulo_2  (.\NÚMERO ({in_5, in_6, in_7, in_8}), .\Módulo (GB));
  \Módulo  \módulo_3  (.\NÚMERO (x), .\Módulo (GX));
  \Módulo  \módulo_4  (.\NÚMERO (y), .\Módulo (GY));
  \Cronômetro_3  \cronômetro_3_1  (
    .INICIAR(START), .CLK(clock_1_out), .RESETAR(RESETAR), .JOGADOR(T), .Jogando(on), ._0A(_0A), ._0B(_0B),
    .out_22(tunnel), .D_min_2(dmb_t), .U_min_2(umb_t), .D_seg_2(dsb_t), .U_seg_2(usb_t), .US_2(USB),
    .DS_2(DSB), .UM_2(UMB), .DM_2(DMB), .D_min(dma_t), .U_min(uma_t), .D_seg(dsa_t), .U_seg(usa_t), .DM(DMA),
    .UM(UMA), .DS(DSA), .US(USA), .CONFIG(CONFIGURAR));
  Clock clock_1 (.out(clock_1_out));
  Jogo_2 jogo_2_1 (
    .X(x), .Y(y), .SCT1(sct1), .SCT2(sct2), .Menor(MENOR), .Igual(IGUAL), .Clk(jogo_2_1_clk), .Maior(MAIOR),
    .\PRÓXIMO (\PRÓXIMO ), .RESETAR(RESETAR), .ACERTOU(ACERTOU), .RES(RES));
  Random #(.width(4)) random_1 (.clk(jogo_2_1_clk), .next(1'b1), .out(sct1));  // open: clr
  Random #(.width(4), .seed(1)) random_2 (.clk(jogo_2_1_clk), .next(1'b1), .out(sct2));  // open: clr
  Button button_10 (.out(DMB));
  Button button_11 (.out(UMB));
  Hex_Digit_Display hex_digit_display_9 (.value(umb_t));  // open: dp
  Hex_Digit_Display hex_digit_display_10 (.value(dmb_t));  // open: dp
  LED led_18 (.in(in_5));
  or or_6 (or_6_out, _0, _1);
  Hex_Digit_Display hex_digit_display_11 (.value(PB));  // open: dp
  Button button_12 (.out(DSB));
  LED led_19 (.in(1'b1));
  LED led_20 (.in(1'b1));
  Hex_Digit_Display hex_digit_display_12 (.value(dsb_t));  // open: dp
  Hex_Digit_Display hex_digit_display_13 (.value(GB));  // open: dp
  LED led_21 (.in(B_JOGANDO));
  \Situação  \situação_1  (.S(S), ._0A(_0A), ._0B(_0B), ._5(_5), ._4(_4), ._3(_3), ._2(_2), ._1(_1), ._0(_0));
  or or_7 (or_7_out, _5, _2);
  and and_9 (RES, or_7_out, on);
  Multiplexer #(.width(4)) multiplexer_1 (
    .in0({in_1, in_2, in_3, in_4}), .in1({in_5, in_6, in_7, in_8}), .out(C), .sel(and_10_out));  // open: en
  and and_10 (and_10_out, ~or_6_out, or_8_out);  // AND_Gate
  or or_8 (or_8_out, _3, _4);
  Button button_13 (.out(USB));
  Hex_Digit_Display hex_digit_display_14 (.value(usb_t));  // open: dp

  // Other names for the same wires on the sheet: A[3:0] = {in_1, in_2, in_3, in_4}; A0 = in_4; A1 = in_3; A2 = in_2;
  //   A3 = in_1; SA = in_1; B[3:0] = {in_5, in_6, in_7, in_8}; B0 = in_8; B1 = in_7; B2 = in_6; B3 = in_5; SB = in_5

  // Notes on the sheet:
  //   JOGADOR - A
  //   JOGADOR - B
endmodule

module \Memória  (
  input  D,
  input  CLK,
  input  CHANGE,
  input  ENABLE,
  input  CLEAR,
  input  PRESET,
  output Q
);

  wire and_1_out, and_2_out, and_3_out, and_4_out, and_5_out, and_6_out, nor_2_out, not_1_out, not_2_out,
       not_3_out, not_4_out, not_5_out, not_6_out, not_7_out, or_1_out;

  not not_1 (not_1_out, not_2_out);
  not not_2 (not_2_out, CLK);
  not not_3 (not_3_out, CHANGE);
  not not_4 (not_4_out, not_3_out);
  and and_1 (and_1_out, CLK, not_5_out);
  not not_5 (not_5_out, not_1_out);
  and and_2 (and_2_out, CHANGE, not_6_out);
  not not_6 (not_6_out, not_4_out);
  and and_3 (and_3_out, and_1_out, ENABLE);
  or or_1 (or_1_out, and_3_out, and_4_out);
  and and_4 (and_4_out, and_2_out, ~ENABLE);  // AND_Gate
  not not_7 (not_7_out, D);
  and and_5 (and_5_out, not_7_out, or_1_out);
  and and_6 (and_6_out, or_1_out, D);
  nor nor_1 (Q, and_5_out, CLEAR, nor_2_out);
  nor nor_2 (nor_2_out, Q, PRESET, and_6_out);
endmodule

module \Cronômetro_1  (
  input  [3:0] N_SOMA,
  input  CHANGE,
  input  CLK,
  input  ENABLE,
  input  CLEAR,
  output [3:0] Display,
  output \Padrão 
);

  wire [3:0] somador_4_bits_1_out_3;

  \Memória  \memória_1  (
    .D(somador_4_bits_1_out_3[3]), .CLK(CLK), .Q(Display[3]), .ENABLE(ENABLE), .CLEAR(CLEAR), .PRESET(1'b0),
    .CHANGE(CHANGE));
  \Memória  \memória_2  (
    .D(somador_4_bits_1_out_3[2]), .CLK(CLK), .Q(Display[2]), .ENABLE(ENABLE), .CLEAR(CLEAR), .PRESET(1'b0),
    .CHANGE(CHANGE));
  \Memória  \memória_3  (
    .D(somador_4_bits_1_out_3[1]), .CLK(CLK), .Q(Display[1]), .ENABLE(ENABLE), .CLEAR(CLEAR), .PRESET(1'b0),
    .CHANGE(CHANGE));
  and and_1 (\Padrão , ~Display[3], ~Display[2], ~Display[1], ~Display[0]);  // AND_Gate
  \Memória  \memória_4  (
    .D(somador_4_bits_1_out_3[0]), .CLK(CLK), .Q(Display[0]), .ENABLE(ENABLE), .CLEAR(CLEAR), .PRESET(1'b0),
    .CHANGE(CHANGE));
  Somador_4_Bits somador_4_bits_1 (.in_1(Display), .in_2(N_SOMA), .out_3(somador_4_bits_1_out_3));  // open: Cout
endmodule

module \Cronômetro_2  (
  input  US,
  input  DS,
  input  UM,
  input  DM,
  input  CLK,
  input  ENABLE,
  input  CLEAR,
  output [3:0] D_min,
  output [3:0] U_min,
  output [3:0] D_seg,
  output [3:0] U_seg,
  output Zerado
);

  wire and_1_out, and_2_out, and_3_out, and_4_out, and_5_out, and_6_out, and_7_out, and_8_out, and_9_out;
  wire [3:0] multiplexer_1_out, multiplexer_2_out, multiplexer_3_out, multiplexer_4_out;
  wire [3:1] not_2_out, not_4_out, not_6_out, not_8_out;

  \Cronômetro_1  \cronômetro_1_1  (
    .N_SOMA(multiplexer_1_out), .CHANGE(US), .CLK(CLK), .\Padrão (not_2_out[3]), .Display(U_seg),
    .ENABLE(ENABLE), .CLEAR(CLEAR));
  Multiplexer #(.width(4)) multiplexer_1 (
    .in0(4'b1111), .in1({not_2_out, not_2_out[3]}), .out(multiplexer_1_out), .sel(not_2_out[3]));  // open: en
  not not_1 (not_2_out[2], not_2_out[3]);
  not not_2 (not_2_out[1], not_2_out[3]);
  and and_1 (and_1_out, ENABLE, and_2_out);
  and and_2 (and_2_out, ~U_seg[0], ~U_seg[1], ~U_seg[2], ~U_seg[3]);  // AND_Gate
  Multiplexer #(.width(4)) multiplexer_2 (
    .in0(4'b1111), .in1({not_4_out, not_4_out[2]}), .out(multiplexer_2_out), .sel(not_4_out[2]));  // open: en
  not not_3 (not_4_out[3], not_4_out[2]);
  not not_4 (not_4_out[1], not_4_out[2]);
  \Cronômetro_1  \cronômetro_1_2  (
    .N_SOMA(multiplexer_2_out), .CHANGE(DS), .CLK(CLK), .\Padrão (not_4_out[2]), .Display(D_seg),
    .ENABLE(and_1_out), .CLEAR(CLEAR));
  and and_3 (and_3_out, ~D_seg[0], ~D_seg[1], ~D_seg[2], ~D_seg[3]);  // AND_Gate
  and and_4 (and_4_out, ENABLE, and_5_out);
  and and_5 (and_5_out, and_3_out, and_2_out);
  \Cronômetro_1  \cronômetro_1_3  (
    .N_SOMA(multiplexer_3_out), .CHANGE(UM), .CLK(CLK), .\Padrão (not_6_out[3]), .Display(U_min),
    .ENABLE(and_4_out), .CLEAR(CLEAR));
  Multiplexer #(.width(4)) multiplexer_3 (
    .in0(4'b1111), .in1({not_6_out, not_6_out[3]}), .out(multiplexer_3_out), .sel(not_6_out[3]));  // open: en
  not not_5 (not_6_out[2], not_6_out[3]);
  not not_6 (not_6_out[1], not_6_out[3]);
  and and_6 (and_6_out, ~U_min[0], ~U_min[1], ~U_min[2], ~U_min[3]);  // AND_Gate
  and and_7 (and_7_out, and_6_out, and_5_out);
  \Cronômetro_1  \cronômetro_1_4  (
    .N_SOMA(multiplexer_4_out), .CHANGE(DM), .CLK(CLK), .\Padrão (not_8_out[2]), .Display(D_min),
    .ENABLE(and_8_out), .CLEAR(CLEAR));
  and and_8 (and_8_out, ENABLE, and_7_out);
  Multiplexer #(.width(4)) multiplexer_4 (
    .in0(4'b1111), .in1({not_8_out, not_8_out[2]}), .out(multiplexer_4_out), .sel(not_8_out[2]));  // open: en
  not not_7 (not_8_out[3], not_8_out[2]);
  not not_8 (not_8_out[1], not_8_out[2]);
  and and_9 (and_9_out, ~D_min[0], ~D_min[1], ~D_min[2], ~D_min[3]);  // AND_Gate
  and and_10 (Zerado, and_9_out, and_7_out);

  // Notes on the sheet:
  //   %
  //   &
  //   %
  //   &
  //   %
  //   &
  //   %
endmodule

module \Cronômetro_3  (
  input  DM,
  input  UM,
  input  DS,
  input  US,
  input  DM_2,
  input  UM_2,
  input  DS_2,
  input  US_2,
  input  CONFIG,
  input  CLK,
  input  RESETAR,
  input  INICIAR,
  input  JOGADOR,
  output [3:0] D_min,
  output [3:0] D_min_2,
  output [3:0] U_min,
  output [3:0] U_min_2,
  output [3:0] D_seg,
  output [3:0] D_seg_2,
  output [3:0] U_seg,
  output [3:0] U_seg_2,
  output out_22,
  output _0A,
  output _0B,
  output Jogando
);

  wire and_1_out, and_2_out, and_3_out, and_4_out, and_5_out, and_6_out, and_7_out, and_8_out, and_9_out,
       and_10_out, not_1_out, not_2_out, or_1_out, or_2_out, or_3_out, or_4_out, or_5_out, or_6_out, or_7_out;

  or or_1 (or_1_out, CONFIG, RESETAR);
  \Memória  \memória_1  (
    .D(or_1_out), .CLK(or_1_out), .Q(out_22), .ENABLE(1'b1), .CLEAR(and_1_out), .PRESET(not_1_out),
    .CHANGE(not_1_out));
  not not_1 (not_1_out, 1'b1);
  and and_1 (and_1_out, ~or_1_out, or_2_out);  // AND_Gate
  or or_2 (or_2_out, Jogando, RESETAR);
  or or_3 (or_3_out, out_22, RESETAR);
  and and_2 (and_2_out, ~INICIAR, or_3_out);  // AND_Gate
  \Memória  \memória_2  (
    .D(INICIAR), .CLK(INICIAR), .Q(Jogando), .ENABLE(1'b1), .CLEAR(and_2_out), .PRESET(not_2_out),
    .CHANGE(not_2_out));
  not not_2 (not_2_out, 1'b1);
  and and_3 (and_3_out, out_22, or_5_out);
  or or_4 (or_4_out, UM_2, UM);
  or or_5 (or_5_out, US_2, US);
  or or_6 (or_6_out, DS_2, DS);
  and and_4 (and_4_out, out_22, or_6_out);
  and and_5 (and_5_out, out_22, or_4_out);
  or or_7 (or_7_out, DM_2, DM);
  and and_6 (and_6_out, out_22, or_7_out);
  \Cronômetro_2  \cronômetro_2_1  (
    .CLK(CLK), .ENABLE(and_7_out), .CLEAR(RESETAR), .Zerado(_0A), .US(and_3_out), .DS(and_4_out),
    .UM(and_5_out), .DM(and_6_out), .D_min(D_min), .U_min(U_min), .D_seg(D_seg), .U_seg(U_seg));
  and and_7 (and_7_out, ~_0A, and_8_out);  // AND_Gate
  and and_8 (and_8_out, Jogando, ~JOGADOR);  // AND_Gate
  and and_9 (and_9_out, and_10_out, ~_0B);  // AND_Gate
  and and_10 (and_10_out, JOGADOR, Jogando);
  \Cronômetro_2  \cronômetro_2_2  (
    .CLK(CLK), .ENABLE(and_9_out), .CLEAR(RESETAR), .Zerado(_0B), .US(and_3_out), .DS(and_4_out),
    .UM(and_5_out), .DM(and_6_out), .D_min(D_min_2), .U_min(U_min_2), .D_seg(D_seg_2), .U_seg(U_seg_2));
endmodule

module Chute (
  input  \PRÓXIMO ,
  input  CLK,
  input  CHUTANDO,
  input  CLEAR,
  input  [3:0] X_Y,
  output [2:0] Estado,
  output Sinal,
  output [3:0] Display,
  output Led
);

  wire and_1_out;
  wire [2:0] multiplexer_1_out, somador_3_bits_1_out_3;

  \Memória  \memória_1  (
    .D(somador_3_bits_1_out_3[0]), .CLK(1'b0), .Q(Estado[0]), .ENABLE(1'b0), .CLEAR(CLEAR), .PRESET(1'b0),
    .CHANGE(\PRÓXIMO ));
  \Memória  \memória_2  (
    .D(somador_3_bits_1_out_3[1]), .CLK(1'b0), .Q(Estado[1]), .ENABLE(1'b0), .CLEAR(CLEAR), .PRESET(1'b0),
    .CHANGE(\PRÓXIMO ));
  \Memória  \memória_3  (
    .D(X_Y[3]), .CLK(CLK), .Q(Display[3]), .ENABLE(CHUTANDO), .CLEAR(CLEAR), .PRESET(1'b0), .CHANGE(1'b0));
  \Memória  \memória_4  (
    .D(X_Y[2]), .CLK(CLK), .Q(Display[2]), .ENABLE(CHUTANDO), .CLEAR(CLEAR), .PRESET(1'b0), .CHANGE(1'b0));
  and and_1 (and_1_out, Estado[0], ~Estado[1], Estado[2]);  // AND_Gate
  \Memória  \memória_5  (
    .D(somador_3_bits_1_out_3[2]), .CLK(1'b0), .Q(Estado[2]), .ENABLE(1'b0), .CLEAR(CLEAR), .PRESET(1'b0),
    .CHANGE(\PRÓXIMO ));
  \Memória  \memória_6  (
    .D(X_Y[1]), .CLK(CLK), .Q(Display[1]), .ENABLE(CHUTANDO), .CLEAR(CLEAR), .PRESET(1'b0), .CHANGE(1'b0));
  Multiplexer #(.width(3)) multiplexer_1 (
    .in0(3'b001), .in1(3'b011), .out(multiplexer_1_out), .sel(and_1_out));  // open: en
  Somador_3_Bits somador_3_bits_1 (.in_1(Estado), .in_2(multiplexer_1_out), .out_3(somador_3_bits_1_out_3));
  \Memória  \memória_7  (
    .D(X_Y[0]), .CLK(CLK), .Q(Display[0]), .ENABLE(CHUTANDO), .CLEAR(CLEAR), .PRESET(1'b0), .CHANGE(1'b0));

  assign Led = CHUTANDO;
  assign Sinal = Display[3];
endmodule

module \Situação  (
  input  [2:0] S,
  input  _0A,
  input  _0B,
  output _5,
  output _4,
  output _3,
  output _2,
  output _1,
  output _0
);

  wire and_1_out, and_2_out, and_3_out, and_4_out, and_5_out, and_6_out, and_7_out, and_8_out, and_9_out,
       and_10_out, and_11_out, and_12_out, and_13_out, and_14_out, and_15_out, and_16_out, and_17_out,
       and_18_out;

  and and_1 (and_1_out, S[2], ~S[1], S[0], ~_0A, _0B);  // AND_Gate
  and and_2 (and_2_out, ~S[2], S[1], S[0], ~_0A, _0B);  // AND_Gate
  and and_3 (and_3_out, S[2], ~S[1], ~S[0], ~_0A, _0B);  // AND_Gate
  and and_4 (and_4_out, ~S[2], ~S[1], S[0], ~_0A, _0B);  // AND_Gate
  and and_5 (and_5_out, ~S[2], S[1], ~S[0], ~_0A, _0B);  // AND_Gate
  and and_6 (and_6_out, ~S[2], ~S[1], ~S[0], ~_0A, _0B);  // AND_Gate
  and and_7 (and_7_out, S[2], ~S[1], S[0], _0A, ~_0B);  // AND_Gate
  and and_8 (and_8_out, S[2], ~S[1], ~S[0], _0A, ~_0B);  // AND_Gate
  and and_9 (and_9_out, ~S[2], S[1], S[0], _0A, ~_0B);  // AND_Gate
  and and_10 (and_10_out, ~S[2], S[1], ~S[0], _0A, ~_0B);  // AND_Gate
  and and_11 (and_11_out, ~S[2], ~S[1], S[0], _0A, ~_0B);  // AND_Gate
  and and_12 (and_12_out, ~S[2], ~S[1], ~S[0], _0A, ~_0B);  // AND_Gate
  and and_13 (and_13_out, S[2], ~S[1], S[0], ~_0A, ~_0B);  // AND_Gate
  and and_14 (and_14_out, S[2], ~S[1], ~S[0], ~_0A, ~_0B);  // AND_Gate
  and and_15 (and_15_out, ~S[2], S[1], S[0], ~_0A, ~_0B);  // AND_Gate
  and and_16 (and_16_out, ~S[2], ~S[1], S[0], ~_0A, ~_0B);  // AND_Gate
  and and_17 (and_17_out, ~S[2], S[1], ~S[0], ~_0A, ~_0B);  // AND_Gate
  and and_18 (and_18_out, ~S[2], ~S[1], ~S[0], ~_0A, ~_0B);  // AND_Gate
  or or_1 (_5, and_10_out, and_7_out, and_13_out);
  or or_2 (_4, and_11_out, and_8_out, and_14_out);
  or or_3 (_3, and_12_out, and_9_out, and_15_out);
  or or_4 (_2, and_1_out, and_5_out, and_17_out);
  or or_5 (_1, and_3_out, and_4_out, and_16_out);
  or or_6 (_0, and_2_out, and_6_out, and_18_out);
endmodule

module Jogo_1 (
  input  [3:0] X,
  input  [3:0] Y,
  input  [3:0] SCT1,
  input  [3:0] SCT2,
  output Menor,
  output Igual,
  output Maior
);

  wire [4:0] n4_para_5_1_soma, n4_para_5_2_soma;

  _4_para_5 u_4_para_5_1 (.in_1(X), .in_2(Y), .Soma(n4_para_5_1_soma));
  _4_para_5 u_4_para_5_2 (.in_1(SCT1), .in_2(SCT2), .Soma(n4_para_5_2_soma));
  comparador comparador_1 (
    .JGD(n4_para_5_1_soma), .SCT(n4_para_5_2_soma), .Menor(Menor), .Acertou(Igual), .Maior(Maior));
endmodule

module Jogo_2 (
  input  [3:0] X,
  input  \PRÓXIMO ,
  input  RESETAR,
  input  [3:0] Y,
  input  [3:0] SCT1,
  input  [3:0] SCT2,
  input  ACERTOU,
  input  RES,
  output Menor,
  output Igual,
  output Clk,
  output Maior
);

  wire and_1_out, jogo_1_1_igual, jogo_1_1_maior, jogo_1_1_menor, \memória_1_q ;

  \Memória  \memória_1  (
    .D(1'b0), .CLK(1'b0), .Q(\memória_1_q ), .ENABLE(1'b0), .CLEAR(\PRÓXIMO ), .PRESET(ACERTOU), .CHANGE(1'b0));
  or or_1 (Clk, RESETAR, and_1_out);
  and and_1 (and_1_out, \PRÓXIMO , \memória_1_q );
  Jogo_1 jogo_1_1 (
    .X(X), .Y(Y), .SCT1(SCT1), .SCT2(SCT2), .Menor(jogo_1_1_menor), .Igual(jogo_1_1_igual),
    .Maior(jogo_1_1_maior));
  and and_2 (Menor, jogo_1_1_menor, RES);
  and and_3 (Igual, jogo_1_1_igual, RES);
  and and_4 (Maior, jogo_1_1_maior, RES);
endmodule

module comparador (
  input  [4:0] JGD,
  input  [4:0] SCT,
  output Menor,
  output Acertou,
  output Maior
);

  wire \_1º_2_out , \_1º_3_out , \_1º_4_out , \_1º_5_out , \_1º_6_out , \_1º_7_out , \_1º_out , \_2º_2_out ,
       \_2º_out , \_3º_2_out , \_3º_out , \_4º_2_out , \_4º_out , and_1_out, and_2_out, and_3_out, and_4_out,
       and_5_out, and_6_out, nor_1_out, or_1_out;

  and \_1º  (\_1º_out , SCT[4], ~JGD[4]);  // AND_Gate
  and \_1º_2  (\_1º_2_out , JGD[4], ~SCT[4]);  // AND_Gate
  and \_1º_3  (\_1º_3_out , JGD[3], ~SCT[3]);  // AND_Gate
  and \_2º  (\_2º_out , JGD[2], ~SCT[2]);  // AND_Gate
  and and_1 (and_1_out, \_2º_out , \_1º_4_out );
  and \_3º  (\_3º_out , JGD[1], ~SCT[1]);  // AND_Gate
  and \_4º  (\_4º_out , JGD[0], ~SCT[0]);  // AND_Gate
  xnor \_1º_4  (\_1º_4_out , JGD[3], SCT[3]);
  and and_2 (and_2_out, \_1º_4_out , \_2º_2_out );
  xnor \_2º_2  (\_2º_2_out , JGD[2], SCT[2]);
  xnor \_3º_2  (\_3º_2_out , JGD[1], SCT[1]);
  xnor \_4º_2  (\_4º_2_out , JGD[0], SCT[0]);
  and and_3 (and_3_out, \_3º_out , and_2_out);
  and and_4 (and_4_out, and_2_out, \_3º_2_out );
  and and_5 (and_5_out, \_4º_out , and_4_out);
  and and_6 (and_6_out, and_4_out, \_4º_2_out );
  and \_1º_5  (\_1º_5_out , ~\_1º_out , ~\_1º_2_out );  // AND_Gate
  or or_1 (or_1_out, \_1º_3_out , and_1_out, and_3_out, and_5_out);
  nor nor_1 (nor_1_out, or_1_out, and_6_out);
  and \_1º_6  (\_1º_6_out , or_1_out, \_1º_5_out );
  and \_1º_7  (\_1º_7_out , nor_1_out, \_1º_5_out );
  or or_2 (Menor, \_1º_out , \_1º_6_out );
  and \_1º_8  (Acertou, \_1º_5_out , and_6_out);
  or or_3 (Maior, \_1º_2_out , \_1º_7_out );
endmodule

module _4_para_5 (
  input  [3:0] in_1,
  input  [3:0] in_2,
  output [4:0] Soma
);

  wire xnor_1_out;
  wire [3:0] \módulo_1_módulo , \módulo_2_módulo , \módulo_3_módulo , somador_4_bits_1_out_3,
       somador_4_bits_2_out_3;
  wire [4:0] multiplexer_1_out, multiplexer_2_out, not_1_out, not_2_out, somador_5_bits_1_out_3,
       somador_5_bits_2_out_3;
  wire [4:4] somador_4_bits_2_cout;

  Somador_4_Bits somador_4_bits_1 (.in_1(in_1), .in_2(in_2), .out_3(somador_4_bits_1_out_3));  // open: Cout
  \Módulo  \módulo_1  (.\NÚMERO (in_1), .\Módulo (\módulo_1_módulo ));
  \Módulo  \módulo_2  (.\NÚMERO (in_2), .\Módulo (\módulo_2_módulo ));
  Somador_4_Bits somador_4_bits_2 (
    .in_1(\módulo_1_módulo ), .in_2(\módulo_2_módulo ), .out_3(somador_4_bits_2_out_3),
    .Cout(somador_4_bits_2_cout[4]));
  \Módulo  \módulo_3  (.\NÚMERO (somador_4_bits_1_out_3), .\Módulo (\módulo_3_módulo ));
  assign not_1_out = ~{1'b0, \módulo_3_módulo };  // NOT_Gate not_1, 5 bits wide
  Somador_5_Bits somador_5_bits_1 (.in_1(not_1_out), .in_2(5'b00001), .out_3(somador_5_bits_1_out_3));
  Somador_5_Bits somador_5_bits_2 (.in_1(not_2_out), .in_2(5'b00001), .out_3(somador_5_bits_2_out_3));
  assign not_2_out = ~{somador_4_bits_2_cout[4], somador_4_bits_2_out_3};  // NOT_Gate not_2, 5 bits wide
  Multiplexer #(.width(5)) multiplexer_1 (
    .in0({1'b0, \módulo_3_módulo }), .in1(somador_5_bits_1_out_3), .out(multiplexer_1_out),
    .sel(somador_4_bits_1_out_3[3]));  // open: en
  Multiplexer #(.width(5)) multiplexer_2 (
    .in0({somador_4_bits_2_cout[4], somador_4_bits_2_out_3}), .in1(somador_5_bits_2_out_3),
    .out(multiplexer_2_out), .sel(in_1[3]));  // open: en
  Multiplexer #(.width(5)) multiplexer_3 (
    .in0(multiplexer_1_out), .in1(multiplexer_2_out), .out(Soma), .sel(xnor_1_out));  // open: en
  xnor xnor_1 (xnor_1_out, in_1[3], in_2[3]);

  // Other names for the same wires on the sheet: A[3:0] = in_1; B[3:0] = in_2
endmodule

module Placar (
  input  AUMENTAR,
  input  CLEAR,
  output Venceu,
  output [3:0] Display
);

  wire [3:0] somador_4_bits_1_out_3;

  and and_1 (Venceu, Display[0], Display[1], Display[2], Display[3]);
  \Memória  \memória_1  (
    .D(somador_4_bits_1_out_3[0]), .CLK(AUMENTAR), .Q(Display[0]), .ENABLE(1'b1), .CLEAR(CLEAR),
    .PRESET(1'b0), .CHANGE(1'b0));
  \Memória  \memória_2  (
    .D(somador_4_bits_1_out_3[1]), .CLK(AUMENTAR), .Q(Display[1]), .ENABLE(1'b1), .CLEAR(CLEAR),
    .PRESET(1'b0), .CHANGE(1'b0));
  \Memória  \memória_3  (
    .D(somador_4_bits_1_out_3[2]), .CLK(AUMENTAR), .Q(Display[2]), .ENABLE(1'b1), .CLEAR(CLEAR),
    .PRESET(1'b0), .CHANGE(1'b0));
  \Memória  \memória_4  (
    .D(somador_4_bits_1_out_3[3]), .CLK(AUMENTAR), .Q(Display[3]), .ENABLE(1'b1), .CLEAR(CLEAR),
    .PRESET(1'b0), .CHANGE(1'b0));
  Somador_4_Bits somador_4_bits_1 (.in_1(Display), .in_2(4'b0001), .out_3(somador_4_bits_1_out_3));  // open: Cout
endmodule

module comparador_simples (
  input  [3:0] in_1,
  input  [3:0] in_2,
  input  FIM_DE_JOGO,
  output Menor,
  output Igual,
  output Maior
);

  wire and_1_out, and_2_out, and_3_out, and_4_out, and_5_out, and_6_out, and_7_out, and_8_out, and_9_out,
       and_10_out, or_1_out, xnor_1_out, xnor_2_out, xnor_3_out, xnor_4_out, xnor_5_out;

  and and_1 (and_1_out, in_1[3], ~in_2[3]);  // AND_Gate
  and and_2 (and_2_out, in_1[2], ~in_2[2]);  // AND_Gate
  and and_3 (and_3_out, and_2_out, xnor_1_out);
  and and_4 (and_4_out, in_1[1], ~in_2[1]);  // AND_Gate
  and and_5 (and_5_out, in_1[0], ~in_2[0]);  // AND_Gate
  xnor xnor_1 (xnor_1_out, in_1[3], in_2[3]);
  and and_6 (and_6_out, xnor_1_out, xnor_2_out);
  xnor xnor_2 (xnor_2_out, in_1[2], in_2[2]);
  xnor xnor_3 (xnor_3_out, in_1[1], in_2[1]);
  xnor xnor_4 (xnor_4_out, in_1[0], in_2[0]);
  and and_7 (and_7_out, and_4_out, and_6_out);
  and and_8 (and_8_out, and_6_out, xnor_3_out);
  and and_9 (and_9_out, and_5_out, and_8_out);
  and and_10 (and_10_out, and_8_out, xnor_4_out);
  or or_1 (or_1_out, and_1_out, and_3_out, and_7_out, and_9_out);
  xnor xnor_5 (xnor_5_out, or_1_out, and_10_out);
  and and_11 (Menor, or_1_out, FIM_DE_JOGO);
  and and_12 (Igual, and_10_out, FIM_DE_JOGO);
  and and_13 (Maior, xnor_5_out, FIM_DE_JOGO);
endmodule

module \Módulo  (
  input  [3:0] \NÚMERO ,
  output [3:0] \Módulo 
);

  wire [3:0] not_1_out, somador_4_bits_1_out_3;

  not not_1 (not_1_out[0], \NÚMERO [0]);
  not not_2 (not_1_out[1], \NÚMERO [1]);
  not not_3 (not_1_out[2], \NÚMERO [2]);
  not not_4 (not_1_out[3], \NÚMERO [3]);
  Somador_4_Bits somador_4_bits_1 (.in_1(not_1_out), .in_2(4'b0001), .out_3(somador_4_bits_1_out_3));  // open: Cout
  Multiplexer #(.width(4)) multiplexer_1 (
    .in0(\NÚMERO ), .in1(somador_4_bits_1_out_3), .out(\Módulo ), .sel(\NÚMERO [3]));  // open: en
endmodule

module Soma_Simples (
  input  A,
  input  B,
  input  Cin,
  output S,
  output Cout
);

  wire and_1_out, and_2_out, xor_1_out;

  xor xor_1 (xor_1_out, A, B);
  and and_1 (and_1_out, xor_1_out, Cin);
  and and_2 (and_2_out, A, B);
  xor xor_2 (S, xor_1_out, Cin);
  or or_1 (Cout, and_1_out, and_2_out);
endmodule

module Somador_3_Bits (
  input  [2:0] in_1,
  input  [2:0] in_2,
  output [2:0] out_3
);

  wire soma_simples_1_cout, soma_simples_2_cout;

  Soma_Simples soma_simples_1 (.A(in_1[0]), .B(in_2[0]), .Cin(1'b0), .S(out_3[0]), .Cout(soma_simples_1_cout));
  Soma_Simples soma_simples_2 (
    .A(in_1[1]), .B(in_2[1]), .Cin(soma_simples_1_cout), .S(out_3[1]), .Cout(soma_simples_2_cout));
  Soma_Simples soma_simples_3 (.A(in_1[2]), .B(in_2[2]), .Cin(soma_simples_2_cout), .S(out_3[2]));  // open: Cout
endmodule

module Somador_4_Bits (
  input  [3:0] in_1,
  input  [3:0] in_2,
  output [3:0] out_3,
  output Cout
);

  wire soma_simples_1_cout, soma_simples_2_cout, soma_simples_3_cout;

  Soma_Simples soma_simples_1 (.A(in_1[0]), .B(in_2[0]), .Cin(1'b0), .S(out_3[0]), .Cout(soma_simples_1_cout));
  Soma_Simples soma_simples_2 (
    .A(in_1[1]), .B(in_2[1]), .Cin(soma_simples_1_cout), .S(out_3[1]), .Cout(soma_simples_2_cout));
  Soma_Simples soma_simples_3 (
    .A(in_1[2]), .B(in_2[2]), .Cin(soma_simples_2_cout), .S(out_3[2]), .Cout(soma_simples_3_cout));
  Soma_Simples soma_simples_4 (.A(in_1[3]), .B(in_2[3]), .Cin(soma_simples_3_cout), .S(out_3[3]), .Cout(Cout));
endmodule

module Somador_5_Bits (
  input  [4:0] in_1,
  input  [4:0] in_2,
  output [4:0] out_3
);

  wire soma_simples_1_cout, soma_simples_2_cout, soma_simples_3_cout, soma_simples_4_cout;

  Soma_Simples soma_simples_1 (.A(in_1[0]), .B(in_2[0]), .Cin(1'b0), .S(out_3[0]), .Cout(soma_simples_1_cout));
  Soma_Simples soma_simples_2 (
    .A(in_1[1]), .B(in_2[1]), .Cin(soma_simples_1_cout), .S(out_3[1]), .Cout(soma_simples_2_cout));
  Soma_Simples soma_simples_3 (
    .A(in_1[2]), .B(in_2[2]), .Cin(soma_simples_2_cout), .S(out_3[2]), .Cout(soma_simples_3_cout));
  Soma_Simples soma_simples_4 (
    .A(in_1[3]), .B(in_2[3]), .Cin(soma_simples_3_cout), .S(out_3[3]), .Cout(soma_simples_4_cout));
  Soma_Simples soma_simples_5 (.A(in_1[4]), .B(in_2[4]), .Cin(soma_simples_4_cout), .S(out_3[4]));  // open: Cout
endmodule
