// Logisim project GTNE.circ as structural Verilog: 21 circuits, main circuit main
module main (
  input  in_1,
  input  in_2,
  input  in_3,
  input  in_4,
  input  in_5,
  input  in_6,
  input  in_7,
  input  in_8
);

  wire _0, _0A, _0B, _1, _2, _3, _4, _5, A_JOGANDO, A_VENCEU, ACERTOU, and_1_out, and_9_out, AWIN, B_JOGANDO,
       B_VENCEU, BWIN, CHUTANDO_X, CHUTANDO_Y, CHUTAR, clock_1_out, comparador_simples_2_acertou,
       comparador_simples_3_acertou, CONFIGURAR, DMA, DMB, DSA, DSB, EMPATE, FIM_DE_JOGO, IGUAL,
       jogo_2_1_clk, MAIOR, MENOR, on, or_1_out, or_3_out, or_4_out, or_5_out, or_6_out, or_8_out, plus_1A,
       plus_1B, PodeX, PodeY, \PRÓXIMO , RES, RESETAR, START, SX, SY, T, tunnel, UMA, UMB, USA, USB;
  wire [2:0] S;
  wire [3:0] C, dma_t, dmb_t, dsa_t, dsb_t, GA, GB, GX, GY, PA, PB, sct1, sct2, uma_t, umb_t, usa_t, usb_t,
       x, y;

  Button button_1 (.out(UMA));
  Button button_2 (.out(DMA));
  Hex_Digit_Display hex_digit_display_1 (.value(uma_t));  // open: dp
  Hex_Digit_Display hex_digit_display_2 (.value(dma_t));  // open: dp
  nand nand_1 (T, on, or_1_out);
  and and_1 (and_1_out, _0A, on, _0B);
  Hex_Digit_Display hex_digit_display_3 (.value(PA));  // open: dp
  LED led_1 (.in(1'b1));
  LED led_2 (.in(1'b1));
  LED led_3 (.in(in_1));
  Hex_Digit_Display hex_digit_display_4 (.value(GA));  // open: dp
  LED led_4 (.in(A_JOGANDO));
  Placar placar_1 (.AUMENTAR(plus_1A), .CLEAR(RESETAR), .out_4(PA), .VENCEU(AWIN));
  and and_2 (A_JOGANDO, or_1_out, on);
  or or_1 (or_1_out, _0, _1, _2);
  or or_2 (FIM_DE_JOGO, and_1_out, or_3_out);
  or or_3 (or_3_out, AWIN, BWIN);
  comparador_simples comparador_simples_1 (
    .in_1(PA), .in_2(PB), .Jogar(FIM_DE_JOGO), .menor(A_VENCEU), .acertou(EMPATE), .maior(B_VENCEU));
  Button button_3 (.out(DSA));
  Button button_4 (.out(USA));
  Hex_Digit_Display hex_digit_display_5 (.value(usa_t));  // open: dp
  Hex_Digit_Display hex_digit_display_6 (.value(dsa_t));  // open: dp
  Placar placar_2 (.AUMENTAR(plus_1B), .CLEAR(RESETAR), .out_4(PB), .VENCEU(BWIN));
  and and_3 (B_JOGANDO, ~or_1_out, on);  // AND_Gate
  and and_4 (PodeX, or_4_out, on);
  or or_4 (or_4_out, _0, _3);
  and and_5 (PodeY, or_5_out, on);
  or or_5 (or_5_out, _1, _4);
  and and_6 (ACERTOU, comparador_simples_2_acertou, RES, comparador_simples_3_acertou);
  comparador_simples comparador_simples_2 (
    .in_1(x), .in_2(sct1), .Jogar(1'b1), .acertou(comparador_simples_2_acertou));  // open: menor, maior
  comparador_simples comparador_simples_3 (
    .in_1(y), .in_2(sct2), .Jogar(1'b1), .acertou(comparador_simples_3_acertou));  // open: menor, maior
  LED led_5 (.in(A_VENCEU));
  Button button_5 (.out(RESETAR));
  LED led_6 (.in(MENOR));
  LED led_7 (.in(SX));
  LED led_8 (.in(FIM_DE_JOGO));
  LED led_9 (.in(EMPATE));
  LED led_10 (.in(tunnel));
  Button button_6 (.out(CONFIGURAR));
  LED led_11 (.in(ACERTOU));
  LED led_12 (.in(IGUAL));
  Button button_7 (.out(CHUTAR));
  Hex_Digit_Display hex_digit_display_7 (.value(GX));  // open: dp
  LED led_13 (.in(CHUTANDO_X));
  Chute chute_1 (
    .CLK(CHUTAR), .\PRÓXIMO (\PRÓXIMO ), .LED(CHUTANDO_X), .Display(x), .CLEAR(RESETAR), .in_5(C),
    .\SITUAÇÃO (S), .Pode(PodeX), .out_7(SX));
  Chute chute_2 (
    .CLK(CHUTAR), .\PRÓXIMO (\PRÓXIMO ), .LED(CHUTANDO_Y), .Display(y), .CLEAR(RESETAR), .in_5(C),
    .\SITUAÇÃO (S), .Pode(PodeY), .out_7(SY));
  and and_7 (plus_1A, ACERTOU, _2);
  and and_8 (plus_1B, ACERTOU, _5);
  Button button_8 (.out(\PRÓXIMO ));
  LED led_14 (.in(SY));
  Hex_Digit_Display hex_digit_display_8 (.value(GY));  // open: dp
  LED led_15 (.in(CHUTANDO_Y));
  LED led_16 (.in(B_VENCEU));
  Button button_9 (.out(START));
  LED led_17 (.in(MAIOR));
  \Módulo  \módulo_1  (.in_1({in_1, in_2, in_3, in_4}), .out_2(GA));
  \Módulo  \módulo_2  (.in_1({in_5, in_6, in_7, in_8}), .out_2(GB));
  \Módulo  \módulo_3  (.in_1(x), .out_2(GX));
  \Módulo  \módulo_4  (.in_1(y), .out_2(GY));
  \Cronômetro_3  \cronômetro_3_1  (
    .CONFIG(CONFIGURAR), .INICIAR(START), .CLK(clock_1_out), .RESETAR(RESETAR), .TROCAR(T), .START(on),
    ._0A(_0A), ._0B(_0B), .out_22(tunnel), .D_MIN_2(dmb_t), .U_MIN_2(umb_t), .D_SEG_2(dsb_t),
    .U_SEG_2(usb_t), .US_2(USB), .DS_2(DSB), .UM_2(UMB), .DM_2(DMB), .D_MIN(dma_t), .U_MIN(uma_t),
    .D_SEG(dsa_t), .U_SEG(usa_t), .DM(DMA), .UM(UMA), .DS(DSA), .US(USA));
  Clock clock_1 (.out(clock_1_out));
  Jogo_2 jogo_2_1 (
    .x(x), .y(y), .sct1(sct1), .sct2(sct2), .menor(MENOR), .igual(IGUAL), .CLK(jogo_2_1_clk), .maior(MAIOR),
    .\Próximo (\PRÓXIMO ), .Resetar(RESETAR), .acertou(ACERTOU), .res(RES));
  Random #(.width(4)) random_1 (.clk(jogo_2_1_clk), .next(1'b1), .out(sct1));  // open: clr
  Random #(.width(4), .seed(1)) random_2 (.clk(jogo_2_1_clk), .next(1'b1), .out(sct2));  // open: clr
  Button button_10 (.out(UMB));
  Button button_11 (.out(DMB));
  Hex_Digit_Display hex_digit_display_9 (.value(dmb_t));  // open: dp
  Hex_Digit_Display hex_digit_display_10 (.value(umb_t));  // open: dp
  LED led_18 (.in(in_5));
  or or_6 (or_6_out, _0, _1);
  Hex_Digit_Display hex_digit_display_11 (.value(PB));  // open: dp
  Button button_12 (.out(DSB));
  LED led_19 (.in(1'b1));
  LED led_20 (.in(1'b1));
  Hex_Digit_Display hex_digit_display_12 (.value(dsb_t));  // open: dp
  Hex_Digit_Display hex_digit_display_13 (.value(GB));  // open: dp
  LED led_21 (.in(B_JOGANDO));
  \Situação  \situação_1  (.S(S), ._0A(_0A), ._0B(_0B), ._5(_5), ._4(_4), ._3(_3), ._2(_2), ._1(_1), ._0(_0));
  or or_7 (RES, _5, _2);
  Multiplexer #(.width(4)) multiplexer_1 (
    .in0({in_1, in_2, in_3, in_4}), .in1({in_5, in_6, in_7, in_8}), .out(C), .sel(and_9_out));  // open: en
  and and_9 (and_9_out, ~or_6_out, or_8_out);  // AND_Gate
  or or_8 (or_8_out, _3, _4);
  Button button_13 (.out(USB));
  Hex_Digit_Display hex_digit_display_14 (.value(usb_t));  // open: dp

  // Other names for the same wires on the sheet: A[3:0] = {in_1, in_2, in_3, in_4}; A0 = in_4; A1 = in_3; A2 = in_2;
  //   A3 = in_1; SA = in_1; B[3:0] = {in_5, in_6, in_7, in_8}; B0 = in_8; B1 = in_7; B2 = in_6; B3 = in_5; SB = in_5

  // Notes on the sheet:
  //   JOGADOR - A
  //   JOGADOR - B
endmodule

module \Memória  (
  input  D,
  input  CLK,
  input  CHANGE,
  input  ENABLE,
  input  CLEAR,
  input  PRESET,
  output Q
);

  wire and_1_out, and_2_out, and_3_out, and_4_out, and_5_out, and_6_out, nor_2_out, not_1_out, not_2_out,
       not_3_out, not_4_out, not_5_out, not_6_out, not_7_out, or_1_out;

  not not_1 (not_1_out, CLK);
  not not_2 (not_2_out, not_1_out);
  not not_3 (not_3_out, not_4_out);
  not not_4 (not_4_out, CHANGE);
  and and_1 (and_1_out, CLK, not_5_out);
  and and_2 (and_2_out, and_1_out, ENABLE);
  not not_5 (not_5_out, not_2_out);
  and and_3 (and_3_out, CHANGE, not_6_out);
  not not_6 (not_6_out, not_3_out);
  or or_1 (or_1_out, and_2_out, and_4_out);
  and and_4 (and_4_out, and_3_out, ~ENABLE);  // AND_Gate
  not not_7 (not_7_out, D);
  and and_5 (and_5_out, not_7_out, or_1_out);
  and and_6 (and_6_out, or_1_out, D);
  nor nor_1 (Q, and_5_out, CLEAR, nor_2_out);
  nor nor_2 (nor_2_out, Q, PRESET, and_6_out);

  // Notes on the sheet:
  //   CHANGE funciona exatamente
  //   como o clock, mas somente quando
  //   o ENABLE está desatvado.
  //   Uma vez que CLK só funciona com ENABLE 1
  //   e CHANGE só com ENABLE 0, no máximo um passará
  //   pelo OU central, impedindo choque de subidas.
endmodule

module \Memória_3_bits  (
  input  D1,
  input  D2,
  input  D3,
  input  CLK,
  input  CLEAR,
  output [2:0] out_6
);

  \Memória  \memória_1  (.D(D1), .CLK(CLK), .Q(out_6[2]), .ENABLE(1'b1), .CLEAR(CLEAR), .PRESET(1'b0), .CHANGE(1'b0));
  \Memória  \memória_2  (.D(D2), .CLK(CLK), .Q(out_6[1]), .ENABLE(1'b1), .CLEAR(CLEAR), .PRESET(1'b0), .CHANGE(1'b0));
  \Memória  \memória_3  (.D(D3), .CLK(CLK), .Q(out_6[0]), .ENABLE(1'b1), .CLEAR(CLEAR), .PRESET(1'b0), .CHANGE(1'b0));
endmodule

module \Cronômetro_1  (
  input  [3:0] n_soma,
  input  CHANGE,
  input  CLK,
  input  ENABLE,
  input  CLEAR,
  output [3:0] Display,
  output \PADRÃO 
);

  wire [3:0] somador_4_bits_1_out_3;

  \Memória  \memória_1  (
    .D(somador_4_bits_1_out_3[3]), .CLK(CLK), .Q(Display[3]), .ENABLE(ENABLE), .CLEAR(CLEAR), .PRESET(1'b0),
    .CHANGE(CHANGE));
  \Memória  \memória_2  (
    .D(somador_4_bits_1_out_3[2]), .CLK(CLK), .Q(Display[2]), .ENABLE(ENABLE), .CLEAR(CLEAR), .PRESET(1'b0),
    .CHANGE(CHANGE));
  \Memória  \memória_3  (
    .D(somador_4_bits_1_out_3[1]), .CLK(CLK), .Q(Display[1]), .ENABLE(ENABLE), .CLEAR(CLEAR), .PRESET(1'b0),
    .CHANGE(CHANGE));
  and and_1 (\PADRÃO , ~Display[3], ~Display[2], ~Display[1], ~Display[0]);  // AND_Gate
  \Memória  \memória_4  (
    .D(somador_4_bits_1_out_3[0]), .CLK(CLK), .Q(Display[0]), .ENABLE(ENABLE), .CLEAR(CLEAR), .PRESET(1'b0),
    .CHANGE(CHANGE));
  Somador_4_Bits somador_4_bits_1 (.in_1(Display), .in_2(n_soma), .out_3(somador_4_bits_1_out_3));  // open: SOBRA

  // Notes on the sheet:
  //   Sempre que o CLK ou o CHANGE forem
  //   acionados, haverá uma incremetação do valor
  //   PADRÃO é utilizada para identificar quando o
  //   display atinge 0, e então vai determinar
  //   para qual valor o display deve ir após isso
  //   Este circuito está sempre incremetando
  //   um certo valor à saída, e então retornando
  //   o resultado para a entrada, funcionando como
  //   cronômetro nesse caso.
endmodule

module \Cronômetro_2  (
  input  US,
  input  DS,
  input  UM,
  input  DM,
  input  CLK,
  input  ENABLE,
  input  CLEAR,
  output [3:0] D_MIN,
  output [3:0] U_MIN,
  output [3:0] D_SEG,
  output [3:0] U_SEG,
  output ZERADO
);

  wire and_1_out, and_2_out, and_3_out, and_4_out, and_5_out, and_6_out, and_7_out, and_8_out, and_9_out;
  wire [3:0] multiplexer_1_out, multiplexer_2_out, multiplexer_3_out, multiplexer_4_out;
  wire [3:1] not_2_out, not_4_out, not_6_out, not_8_out;

  \Cronômetro_1  \cronômetro_1_1  (
    .n_soma(multiplexer_1_out), .CHANGE(US), .CLK(CLK), .\PADRÃO (not_2_out[3]), .Display(U_SEG),
    .ENABLE(ENABLE), .CLEAR(CLEAR));
  Multiplexer #(.width(4)) multiplexer_1 (
    .in0(4'b1111), .in1({not_2_out, not_2_out[3]}), .out(multiplexer_1_out), .sel(not_2_out[3]));  // open: en
  not not_1 (not_2_out[2], not_2_out[3]);
  not not_2 (not_2_out[1], not_2_out[3]);
  and and_1 (and_1_out, ENABLE, and_2_out);
  and and_2 (and_2_out, ~U_SEG[0], ~U_SEG[1], ~U_SEG[2], ~U_SEG[3]);  // AND_Gate
  Multiplexer #(.width(4)) multiplexer_2 (
    .in0(4'b1111), .in1({not_4_out, not_4_out[2]}), .out(multiplexer_2_out), .sel(not_4_out[2]));  // open: en
  not not_3 (not_4_out[3], not_4_out[2]);
  not not_4 (not_4_out[1], not_4_out[2]);
  \Cronômetro_1  \cronômetro_1_2  (
    .n_soma(multiplexer_2_out), .CHANGE(DS), .CLK(CLK), .\PADRÃO (not_4_out[2]), .Display(D_SEG),
    .ENABLE(and_1_out), .CLEAR(CLEAR));
  and and_3 (and_3_out, ~D_SEG[0], ~D_SEG[1], ~D_SEG[2], ~D_SEG[3]);  // AND_Gate
  and and_4 (and_4_out, ENABLE, and_5_out);
  and and_5 (and_5_out, and_3_out, and_2_out);
  \Cronômetro_1  \cronômetro_1_3  (
    .n_soma(multiplexer_3_out), .CHANGE(UM), .CLK(CLK), .\PADRÃO (not_6_out[3]), .Display(U_MIN),
    .ENABLE(and_4_out), .CLEAR(CLEAR));
  Multiplexer #(.width(4)) multiplexer_3 (
    .in0(4'b1111), .in1({not_6_out, not_6_out[3]}), .out(multiplexer_3_out), .sel(not_6_out[3]));  // open: en
  not not_5 (not_6_out[2], not_6_out[3]);
  not not_6 (not_6_out[1], not_6_out[3]);
  and and_6 (and_6_out, ~U_MIN[0], ~U_MIN[1], ~U_MIN[2], ~U_MIN[3]);  // AND_Gate
  and and_7 (and_7_out, and_6_out, and_5_out);
  \Cronômetro_1  \cronômetro_1_4  (
    .n_soma(multiplexer_4_out), .CHANGE(DM), .CLK(CLK), .\PADRÃO (not_8_out[2]), .Display(D_MIN),
    .ENABLE(and_8_out), .CLEAR(CLEAR));
  and and_8 (and_8_out, ENABLE, and_7_out);
  Multiplexer #(.width(4)) multiplexer_4 (
    .in0(4'b1111), .in1({not_8_out, not_8_out[2]}), .out(multiplexer_4_out), .sel(not_8_out[2]));  // open: en
  not not_7 (not_8_out[3], not_8_out[2]);
  not not_8 (not_8_out[1], not_8_out[2]);
  and and_9 (and_9_out, ~D_MIN[0], ~D_MIN[1], ~D_MIN[2], ~D_MIN[3]);  // AND_Gate
  and and_10 (ZERADO, and_9_out, and_7_out);

  // Notes on the sheet:
  //   %
  //   &
  //   Essas são as variáveis de controle. Pelo definição do CHANGE, só funcionam quando ENABLE está desativado.
  //   Ao acionar uma dessas entradas, o valor correspondente no cronômetro decrementa, possibilitando a alteração do cronômetro.
  //   %
  //   &
  //   Essa parte do cronômetro controla a mudança de cada dígito do cronômetro somente quando os dígitos menos significtivos atingem 0 simultaneamente.
  //   As portas AND indicadas com "%" identificam quando o dígito corresponde está em 0.
  //   As portas AND indicadas com "&" fazem esse controle de quando os dígito anteriores atingem 0, juntamente com o ENABLE ativado. Quando ambos ocorrem, elas ativam o ENABLE do dígito correspondente.
  //   %
  //   &
  //   %
  //   Os multiplexadores sempre retornam f para o somador
  //   (decrementando o dígito), exceto quando ele atinge 0,
  //   o que leva a retornar 9 para unidades e 6 para dezenas
endmodule

module \Cronômetro_3  (
  input  DM,
  input  UM,
  input  DS,
  input  US,
  input  DM_2,
  input  UM_2,
  input  DS_2,
  input  US_2,
  input  CONFIG,
  input  CLK,
  input  RESETAR,
  input  INICIAR,
  input  TROCAR,
  output [3:0] D_MIN,
  output [3:0] D_MIN_2,
  output [3:0] U_MIN,
  output [3:0] U_MIN_2,
  output [3:0] D_SEG,
  output [3:0] D_SEG_2,
  output [3:0] U_SEG,
  output [3:0] U_SEG_2,
  output out_22,
  output _0A,
  output _0B,
  output START
);

  wire and_1_out, and_2_out, and_3_out, and_4_out, and_5_out, and_6_out, and_7_out, and_8_out, and_9_out,
       and_10_out, not_1_out, not_2_out, or_1_out, or_2_out, or_3_out, or_4_out, or_5_out, or_6_out, or_7_out;

  or or_1 (or_1_out, CONFIG, RESETAR);
  \Memória  \memória_1  (
    .D(or_1_out), .CLK(or_1_out), .Q(out_22), .ENABLE(1'b1), .CLEAR(and_1_out), .PRESET(not_1_out),
    .CHANGE(not_1_out));
  not not_1 (not_1_out, 1'b1);
  and and_1 (and_1_out, ~or_1_out, or_2_out);  // AND_Gate
  or or_2 (or_2_out, START, RESETAR);
  or or_3 (or_3_out, out_22, RESETAR);
  and and_2 (and_2_out, ~INICIAR, or_3_out);  // AND_Gate
  \Memória  \memória_2  (
    .D(INICIAR), .CLK(INICIAR), .Q(START), .ENABLE(1'b1), .CLEAR(and_2_out), .PRESET(not_2_out),
    .CHANGE(not_2_out));
  not not_2 (not_2_out, 1'b1);
  and and_3 (and_3_out, out_22, or_4_out);
  or or_4 (or_4_out, US_2, US);
  or or_5 (or_5_out, UM_2, UM);
  or or_6 (or_6_out, DS_2, DS);
  and and_4 (and_4_out, out_22, or_5_out);
  and and_5 (and_5_out, out_22, or_6_out);
  or or_7 (or_7_out, DM_2, DM);
  and and_6 (and_6_out, out_22, or_7_out);
  \Cronômetro_2  \cronômetro_2_1  (
    .CLK(CLK), .ENABLE(and_7_out), .CLEAR(RESETAR), .ZERADO(_0A), .US(and_3_out), .DS(and_5_out),
    .UM(and_4_out), .DM(and_6_out), .D_MIN(D_MIN), .U_MIN(U_MIN), .D_SEG(D_SEG), .U_SEG(U_SEG));
  and and_7 (and_7_out, ~_0A, and_8_out);  // AND_Gate
  and and_8 (and_8_out, START, ~TROCAR);  // AND_Gate
  and and_9 (and_9_out, and_10_out, ~_0B);  // AND_Gate
  and and_10 (and_10_out, TROCAR, START);
  \Cronômetro_2  \cronômetro_2_2  (
    .CLK(CLK), .ENABLE(and_9_out), .CLEAR(RESETAR), .ZERADO(_0B), .US(and_3_out), .DS(and_5_out),
    .UM(and_4_out), .DM(and_6_out), .D_MIN(D_MIN_2), .U_MIN(U_MIN_2), .D_SEG(D_SEG_2), .U_SEG(U_SEG_2));

  // Notes on the sheet:
  //   CONFIG e INICIAR saõ ambos 0 inicialmente
  //   CONFIG  e INICIAR se complementam.
  //   Ao ser ativado, CONFIG funciona como entrada
  //   e pulso da memória, guardando 1 na saída
  //   e possibilitando a mudança no cronômetro
  //   Quando INICIAR é ativado, sua saída será 1
  //   Então, ao RESETAR, o CLEAR de ambos é acionado
  //   e como CONFIG estará em 0, sua memória será limpada
  //   Então guardará 0 na saída, impossibilitando a mudança
  //   Quando INICIAR foi ativdo e TROCAR está em 0, o ENABLE do primeiro cronômetro fica acionado
  //   Já quando TROCAR está em 1, o ENABLE do segundo é acionado
  //   Se CONFIG foi acionado, INICIAR retorna 0 e ambos os cronômetros ficam parados
  //   As portas OU abaixo fazem com que
  //   as mudanças nos cronômetros sejam simultâneas
  //   As portas AND só permitem a mudança se CONFIG está ativado
  //   RESETAR também ativa o CLEAR
  //   de ambos os cronômetros
endmodule

module Placar (
  input  AUMENTAR,
  input  CLEAR,
  output VENCEU,
  output [3:0] out_4
);

  wire [3:0] somador_4_bits_1_out_3;

  and and_1 (VENCEU, out_4[0], out_4[1], out_4[2], out_4[3]);
  \Memória  \memória_1  (
    .D(somador_4_bits_1_out_3[0]), .CLK(AUMENTAR), .Q(out_4[0]), .ENABLE(1'b1), .CLEAR(CLEAR), .PRESET(1'b0),
    .CHANGE(1'b0));
  \Memória  \memória_2  (
    .D(somador_4_bits_1_out_3[1]), .CLK(AUMENTAR), .Q(out_4[1]), .ENABLE(1'b1), .CLEAR(CLEAR), .PRESET(1'b0),
    .CHANGE(1'b0));
  \Memória  \memória_3  (
    .D(somador_4_bits_1_out_3[2]), .CLK(AUMENTAR), .Q(out_4[2]), .ENABLE(1'b1), .CLEAR(CLEAR), .PRESET(1'b0),
    .CHANGE(1'b0));
  \Memória  \memória_4  (
    .D(somador_4_bits_1_out_3[3]), .CLK(AUMENTAR), .Q(out_4[3]), .ENABLE(1'b1), .CLEAR(CLEAR), .PRESET(1'b0),
    .CHANGE(1'b0));
  Somador_4_Bits somador_4_bits_1 (.in_1(out_4), .in_2(4'b0001), .out_3(somador_4_bits_1_out_3));  // open: SOBRA
endmodule

module decode (
  input  [3:0] in_1,
  output b,
  output a,
  output f,
  output g,
  output e,
  output d,
  output c
);

  wire _0_out, _1_out, _2_out, _3_out, _4_out, _5_out, _6_out, _7_out, _8_out, _9_out, A_2_out, B_2_out,
       C_2_out, D_2_out, E_2_out, F_2_out;

  or u_b (b, F_2_out, _0_out, _1_out, _2_out, _3_out, _4_out, _7_out, _8_out, _9_out, C_2_out, D_2_out, E_2_out);
  or u_a (a, _0_out, _2_out, _3_out, _5_out, _6_out, _7_out, _8_out, _9_out, A_2_out, B_2_out, D_2_out, E_2_out);
  or u_f (f, _0_out, _4_out, _5_out, _6_out, _8_out, A_2_out, B_2_out, C_2_out);
  or u_g (g, _2_out, _3_out, _4_out, _5_out, _6_out, _8_out, A_2_out, B_2_out, C_2_out, D_2_out, E_2_out);
  or u_e (e, _0_out, _2_out, _6_out, _8_out, A_2_out, E_2_out);
  or u_d (d, _0_out, _2_out, _3_out, _5_out, _6_out, _8_out, A_2_out, B_2_out, D_2_out, E_2_out);
  or u_c (c, D_2_out, _0_out, _1_out, _3_out, _4_out, _5_out, _6_out, F_2_out, _7_out, _8_out, _9_out, A_2_out, B_2_out, C_2_out);
  and F_2 (F_2_out, in_1[3], in_1[2], in_1[1], in_1[0]);
  and E_2 (E_2_out, in_1[3], in_1[2], in_1[1], ~in_1[0]);  // AND_Gate
  and D_2 (D_2_out, in_1[3], in_1[2], ~in_1[1], in_1[0]);  // AND_Gate
  and B_2 (B_2_out, in_1[3], ~in_1[2], in_1[1], in_1[0]);  // AND_Gate
  and C_2 (C_2_out, in_1[3], in_1[2], ~in_1[1], ~in_1[0]);  // AND_Gate
  and _9 (_9_out, in_1[3], ~in_1[2], ~in_1[1], in_1[0]);  // AND_Gate
  and A_2 (A_2_out, in_1[3], ~in_1[2], in_1[1], ~in_1[0]);  // AND_Gate
  and _8 (_8_out, in_1[3], ~in_1[2], ~in_1[1], ~in_1[0]);  // AND_Gate
  and _7 (_7_out, ~in_1[3], in_1[2], in_1[1], in_1[0]);  // AND_Gate
  and _6 (_6_out, ~in_1[3], in_1[2], in_1[1], ~in_1[0]);  // AND_Gate
  and _5 (_5_out, ~in_1[3], in_1[2], ~in_1[1], in_1[0]);  // AND_Gate
  and _4 (_4_out, ~in_1[3], in_1[2], ~in_1[1], ~in_1[0]);  // AND_Gate
  and _3 (_3_out, ~in_1[3], ~in_1[2], in_1[1], in_1[0]);  // AND_Gate
  and _2 (_2_out, ~in_1[3], ~in_1[2], in_1[1], ~in_1[0]);  // AND_Gate
  and _1 (_1_out, ~in_1[3], ~in_1[2], ~in_1[1], in_1[0]);  // AND_Gate
  and _0 (_0_out, ~in_1[3], ~in_1[2], ~in_1[1], ~in_1[0]);  // AND_Gate
endmodule

module Chute (
  input  \PRÓXIMO ,
  input  CLK,
  input  Pode,
  input  CLEAR,
  input  [3:0] in_5,
  output [2:0] \SITUAÇÃO ,
  output out_7,
  output [3:0] Display,
  output LED
);

  wire and_1_out;
  wire [2:0] multiplexer_1_out, somador_3_bits_1_out_3;

  \Memória  \memória_1  (
    .D(in_5[3]), .CLK(CLK), .Q(Display[3]), .ENABLE(Pode), .CLEAR(CLEAR), .PRESET(1'b0), .CHANGE(1'b0));
  \Memória  \memória_2  (
    .D(in_5[2]), .CLK(CLK), .Q(Display[2]), .ENABLE(Pode), .CLEAR(CLEAR), .PRESET(1'b0), .CHANGE(1'b0));
  \Memória  \memória_3  (
    .D(somador_3_bits_1_out_3[0]), .CLK(1'b0), .Q(\SITUAÇÃO [0]), .ENABLE(1'b0), .CLEAR(CLEAR),
    .PRESET(1'b0), .CHANGE(\PRÓXIMO ));
  \Memória  \memória_4  (
    .D(in_5[1]), .CLK(CLK), .Q(Display[1]), .ENABLE(Pode), .CLEAR(CLEAR), .PRESET(1'b0), .CHANGE(1'b0));
  \Memória  \memória_5  (
    .D(somador_3_bits_1_out_3[1]), .CLK(1'b0), .Q(\SITUAÇÃO [1]), .ENABLE(1'b0), .CLEAR(CLEAR),
    .PRESET(1'b0), .CHANGE(\PRÓXIMO ));
  \Memória  \memória_6  (
    .D(in_5[0]), .CLK(CLK), .Q(Display[0]), .ENABLE(Pode), .CLEAR(CLEAR), .PRESET(1'b0), .CHANGE(1'b0));
  and and_1 (and_1_out, \SITUAÇÃO [0], ~\SITUAÇÃO [1], \SITUAÇÃO [2]);  // AND_Gate
  \Memória  \memória_7  (
    .D(somador_3_bits_1_out_3[2]), .CLK(1'b0), .Q(\SITUAÇÃO [2]), .ENABLE(1'b0), .CLEAR(CLEAR),
    .PRESET(1'b0), .CHANGE(\PRÓXIMO ));
  Multiplexer #(.width(3)) multiplexer_1 (
    .in0(3'b001), .in1(3'b011), .out(multiplexer_1_out), .sel(and_1_out));  // open: en
  Somador_3_Bits somador_3_bits_1 (.in_1(\SITUAÇÃO ), .in_2(multiplexer_1_out), .out_3(somador_3_bits_1_out_3));

  assign LED = Pode;
  assign out_7 = Display[3];
endmodule

module comparador (
  input  [4:0] JGD,
  input  [4:0] SCT,
  output MENOR,
  output ACERTOU,
  output MAIOR
);

  wire \_1º_2_out , \_1º_3_out , \_1º_4_out , \_1º_5_out , \_1º_6_out , \_1º_7_out , \_1º_out , \_2º_2_out ,
       \_2º_out , \_3º_2_out , \_3º_out , \_4º_2_out , \_4º_out , and_1_out, and_2_out, and_3_out, and_4_out,
       and_5_out, and_6_out, nor_1_out, or_1_out;

  and \_1º  (\_1º_out , SCT[4], ~JGD[4]);  // AND_Gate
  and \_1º_2  (\_1º_2_out , JGD[4], ~SCT[4]);  // AND_Gate
  and \_1º_3  (\_1º_3_out , JGD[3], ~SCT[3]);  // AND_Gate
  and \_2º  (\_2º_out , JGD[2], ~SCT[2]);  // AND_Gate
  and and_1 (and_1_out, \_2º_out , \_1º_4_out );
  and \_3º  (\_3º_out , JGD[1], ~SCT[1]);  // AND_Gate
  and \_4º  (\_4º_out , JGD[0], ~SCT[0]);  // AND_Gate
  xnor \_1º_4  (\_1º_4_out , JGD[3], SCT[3]);
  and and_2 (and_2_out, \_1º_4_out , \_2º_2_out );
  xnor \_2º_2  (\_2º_2_out , JGD[2], SCT[2]);
  xnor \_3º_2  (\_3º_2_out , JGD[1], SCT[1]);
  xnor \_4º_2  (\_4º_2_out , JGD[0], SCT[0]);
  and and_3 (and_3_out, \_3º_out , and_2_out);
  and and_4 (and_4_out, and_2_out, \_3º_2_out );
  and and_5 (and_5_out, \_4º_out , and_4_out);
  and and_6 (and_6_out, and_4_out, \_4º_2_out );
  and \_1º_5  (\_1º_5_out , ~\_1º_out , ~\_1º_2_out );  // AND_Gate
  or or_1 (or_1_out, \_1º_3_out , and_1_out, and_3_out, and_5_out);
  nor nor_1 (nor_1_out, or_1_out, and_6_out);
  and \_1º_6  (\_1º_6_out , or_1_out, \_1º_5_out );
  and \_1º_7  (\_1º_7_out , nor_1_out, \_1º_5_out );
  or or_2 (MENOR, \_1º_out , \_1º_6_out );
  and \_1º_8  (ACERTOU, \_1º_5_out , and_6_out);
  or or_3 (MAIOR, \_1º_2_out , \_1º_7_out );
endmodule

module Soma_Simples (
  input  A,
  input  B,
  input  Cin,
  output S,
  output Cout
);

  wire and_1_out, and_2_out, xor_1_out;

  xor xor_1 (xor_1_out, A, B);
  and and_1 (and_1_out, xor_1_out, Cin);
  and and_2 (and_2_out, A, B);
  xor xor_2 (S, xor_1_out, Cin);
  or or_1 (Cout, and_1_out, and_2_out);
endmodule

module Somador_4_Bits (
  input  [3:0] in_1,
  input  [3:0] in_2,
  output [3:0] out_3,
  output SOBRA
);

  wire soma_simples_1_cout, soma_simples_2_cout, soma_simples_3_cout;

  Soma_Simples soma_simples_1 (.A(in_1[0]), .B(in_2[0]), .Cin(1'b0), .S(out_3[0]), .Cout(soma_simples_1_cout));
  Soma_Simples soma_simples_2 (
    .A(in_1[1]), .B(in_2[1]), .Cin(soma_simples_1_cout), .S(out_3[1]), .Cout(soma_simples_2_cout));
  Soma_Simples soma_simples_3 (
    .A(in_1[2]), .B(in_2[2]), .Cin(soma_simples_2_cout), .S(out_3[2]), .Cout(soma_simples_3_cout));
  Soma_Simples soma_simples_4 (.A(in_1[3]), .B(in_2[3]), .Cin(soma_simples_3_cout), .S(out_3[3]), .Cout(SOBRA));
endmodule

module Somador_3_Bits (
  input  [2:0] in_1,
  input  [2:0] in_2,
  output [2:0] out_3
);

  wire soma_simples_1_cout, soma_simples_2_cout;

  Soma_Simples soma_simples_1 (.A(in_1[0]), .B(in_2[0]), .Cin(1'b0), .S(out_3[0]), .Cout(soma_simples_1_cout));
  Soma_Simples soma_simples_2 (
    .A(in_1[1]), .B(in_2[1]), .Cin(soma_simples_1_cout), .S(out_3[1]), .Cout(soma_simples_2_cout));
  Soma_Simples soma_simples_3 (.A(in_1[2]), .B(in_2[2]), .Cin(soma_simples_2_cout), .S(out_3[2]));  // open: Cout
endmodule

module Somador_de_2_Bits (
  input  [1:0] in_1,
  input  [1:0] in_2,
  output [1:0] out_3
);

  wire soma_simples_1_cout;

  Soma_Simples soma_simples_1 (.A(in_1[0]), .B(in_2[0]), .Cin(1'b0), .S(out_3[0]), .Cout(soma_simples_1_cout));
  Soma_Simples soma_simples_2 (.A(in_1[1]), .B(in_2[1]), .Cin(soma_simples_1_cout), .S(out_3[1]));  // open: Cout
endmodule

module \Situação  (
  input  [2:0] S,
  input  _0A,
  input  _0B,
  output _5,
  output _4,
  output _3,
  output _2,
  output _1,
  output _0
);

  wire and_1_out, and_2_out, and_3_out, and_4_out, and_5_out, and_6_out, and_7_out, and_8_out, and_9_out,
       and_10_out, and_11_out, and_12_out, and_13_out, and_14_out, and_15_out, and_16_out, and_17_out,
       and_18_out;

  and and_1 (and_1_out, S[2], ~S[1], S[0], ~_0A, _0B);  // AND_Gate
  and and_2 (and_2_out, ~S[2], S[1], S[0], ~_0A, _0B);  // AND_Gate
  and and_3 (and_3_out, S[2], ~S[1], ~S[0], ~_0A, _0B);  // AND_Gate
  and and_4 (and_4_out, ~S[2], ~S[1], S[0], ~_0A, _0B);  // AND_Gate
  and and_5 (and_5_out, ~S[2], S[1], ~S[0], ~_0A, _0B);  // AND_Gate
  and and_6 (and_6_out, ~S[2], ~S[1], ~S[0], ~_0A, _0B);  // AND_Gate
  and and_7 (and_7_out, S[2], ~S[1], S[0], _0A, ~_0B);  // AND_Gate
  and and_8 (and_8_out, ~S[2], S[1], S[0], _0A, ~_0B);  // AND_Gate
  and and_9 (and_9_out, S[2], ~S[1], ~S[0], _0A, ~_0B);  // AND_Gate
  and and_10 (and_10_out, ~S[2], S[1], ~S[0], _0A, ~_0B);  // AND_Gate
  and and_11 (and_11_out, ~S[2], ~S[1], S[0], _0A, ~_0B);  // AND_Gate
  and and_12 (and_12_out, ~S[2], ~S[1], ~S[0], _0A, ~_0B);  // AND_Gate
  and and_13 (and_13_out, S[2], ~S[1], S[0], ~_0A, ~_0B);  // AND_Gate
  and and_14 (and_14_out, ~S[2], S[1], S[0], ~_0A, ~_0B);  // AND_Gate
  and and_15 (and_15_out, S[2], ~S[1], ~S[0], ~_0A, ~_0B);  // AND_Gate
  and and_16 (and_16_out, ~S[2], S[1], ~S[0], ~_0A, ~_0B);  // AND_Gate
  and and_17 (and_17_out, ~S[2], ~S[1], S[0], ~_0A, ~_0B);  // AND_Gate
  and and_18 (and_18_out, ~S[2], ~S[1], ~S[0], ~_0A, ~_0B);  // AND_Gate
  or or_1 (_5, and_10_out, and_7_out, and_13_out);
  or or_2 (_4, and_11_out, and_9_out, and_15_out);
  or or_3 (_3, and_12_out, and_8_out, and_14_out);
  or or_4 (_2, and_1_out, and_5_out, and_16_out);
  or or_5 (_1, and_3_out, and_4_out, and_17_out);
  or or_6 (_0, and_2_out, and_6_out, and_18_out);
endmodule

module comparador_simples (
  input  [3:0] in_1,
  input  [3:0] in_2,
  input  Jogar,
  output menor,
  output acertou,
  output maior
);

  wire and_1_out, and_2_out, and_3_out, and_4_out, and_5_out, and_6_out, and_7_out, and_8_out, and_9_out,
       and_10_out, or_1_out, xnor_1_out, xnor_2_out, xnor_3_out, xnor_4_out, xnor_5_out;

  and and_1 (and_1_out, in_1[3], ~in_2[3]);  // AND_Gate
  and and_2 (and_2_out, in_1[2], ~in_2[2]);  // AND_Gate
  and and_3 (and_3_out, and_2_out, xnor_1_out);
  and and_4 (and_4_out, in_1[1], ~in_2[1]);  // AND_Gate
  and and_5 (and_5_out, in_1[0], ~in_2[0]);  // AND_Gate
  xnor xnor_1 (xnor_1_out, in_1[3], in_2[3]);
  and and_6 (and_6_out, xnor_1_out, xnor_2_out);
  xnor xnor_2 (xnor_2_out, in_1[2], in_2[2]);
  xnor xnor_3 (xnor_3_out, in_1[1], in_2[1]);
  xnor xnor_4 (xnor_4_out, in_1[0], in_2[0]);
  and and_7 (and_7_out, and_4_out, and_6_out);
  and and_8 (and_8_out, and_6_out, xnor_3_out);
  and and_9 (and_9_out, and_5_out, and_8_out);
  and and_10 (and_10_out, and_8_out, xnor_4_out);
  or or_1 (or_1_out, and_1_out, and_3_out, and_7_out, and_9_out);
  xnor xnor_5 (xnor_5_out, or_1_out, and_10_out);
  and and_11 (menor, or_1_out, Jogar);
  and and_12 (acertou, and_10_out, Jogar);
  and and_13 (maior, xnor_5_out, Jogar);
endmodule

module Jogo_2 (
  input  [3:0] x,
  input  \Próximo ,
  input  Resetar,
  input  [3:0] y,
  input  [3:0] sct1,
  input  [3:0] sct2,
  input  acertou,
  input  res,
  output menor,
  output igual,
  output CLK,
  output maior
);

  wire and_1_out, jogo_1_1_igual, jogo_1_1_maior, jogo_1_1_menor, \memória_1_q ;

  \Memória  \memória_1  (
    .D(1'b0), .CLK(1'b0), .Q(\memória_1_q ), .ENABLE(1'b0), .CLEAR(\Próximo ), .PRESET(acertou), .CHANGE(1'b0));
  or or_1 (CLK, Resetar, and_1_out);
  and and_1 (and_1_out, \Próximo , \memória_1_q );
  Jogo_1 jogo_1_1 (
    .in_1(x), .in_2(y), .in_3(sct1), .in_4(sct2), .MENOR(jogo_1_1_menor), .IGUAL(jogo_1_1_igual),
    .MAIOR(jogo_1_1_maior));
  and and_2 (menor, jogo_1_1_menor, res);
  and and_3 (igual, jogo_1_1_igual, res);
  and and_4 (maior, jogo_1_1_maior, res);
endmodule

module Somador_5_Bits (
  input  [4:0] in_1,
  input  [4:0] in_2,
  output [4:0] out_3
);

  wire soma_simples_1_cout, soma_simples_2_cout, soma_simples_3_cout, soma_simples_4_cout;

  Soma_Simples soma_simples_1 (.A(in_1[0]), .B(in_2[0]), .Cin(1'b0), .S(out_3[0]), .Cout(soma_simples_1_cout));
  Soma_Simples soma_simples_2 (
    .A(in_1[1]), .B(in_2[1]), .Cin(soma_simples_1_cout), .S(out_3[1]), .Cout(soma_simples_2_cout));
  Soma_Simples soma_simples_3 (
    .A(in_1[2]), .B(in_2[2]), .Cin(soma_simples_2_cout), .S(out_3[2]), .Cout(soma_simples_3_cout));
  Soma_Simples soma_simples_4 (
    .A(in_1[3]), .B(in_2[3]), .Cin(soma_simples_3_cout), .S(out_3[3]), .Cout(soma_simples_4_cout));
  Soma_Simples soma_simples_5 (.A(in_1[4]), .B(in_2[4]), .Cin(soma_simples_4_cout), .S(out_3[4]));  // open: Cout
endmodule

module _4_para_5 (
  input  [3:0] in_1,
  input  [3:0] in_2,
  output [4:0] out_3
);

  wire xnor_1_out;
  wire [3:0] \módulo_1_out_2 , \módulo_2_out_2 , \módulo_3_out_2 , somador_4_bits_1_out_3,
       somador_4_bits_2_out_3;
  wire [4:0] multiplexer_1_out, multiplexer_2_out, not_1_out, not_2_out, somador_5_bits_1_out_3,
       somador_5_bits_2_out_3;
  wire [4:4] somador_4_bits_2_sobra;

  \Módulo  \módulo_1  (.in_1(in_1), .out_2(\módulo_1_out_2 ));
  xnor xnor_1 (xnor_1_out, in_1[3], in_2[3]);
  \Módulo  \módulo_2  (.in_1(in_2), .out_2(\módulo_2_out_2 ));
  Somador_4_Bits somador_4_bits_1 (.in_1(in_1), .in_2(in_2), .out_3(somador_4_bits_1_out_3));  // open: SOBRA
  Somador_4_Bits somador_4_bits_2 (
    .in_1(\módulo_1_out_2 ), .in_2(\módulo_2_out_2 ), .out_3(somador_4_bits_2_out_3),
    .SOBRA(somador_4_bits_2_sobra[4]));
  \Módulo  \módulo_3  (.in_1(somador_4_bits_1_out_3), .out_2(\módulo_3_out_2 ));
  Somador_5_Bits somador_5_bits_1 (.in_1(not_1_out), .in_2(5'b00001), .out_3(somador_5_bits_1_out_3));
  assign not_1_out = ~{1'b0, \módulo_3_out_2 };  // NOT_Gate not_1, 5 bits wide
  assign not_2_out = ~{somador_4_bits_2_sobra[4], somador_4_bits_2_out_3};  // NOT_Gate not_2, 5 bits wide
  Somador_5_Bits somador_5_bits_2 (.in_1(not_2_out), .in_2(5'b00001), .out_3(somador_5_bits_2_out_3));
  Multiplexer #(.width(5)) multiplexer_1 (
    .in0({1'b0, \módulo_3_out_2 }), .in1(somador_5_bits_1_out_3), .out(multiplexer_1_out),
    .sel(somador_4_bits_1_out_3[3]));  // open: en
  Multiplexer #(.width(5)) multiplexer_2 (
    .in0({somador_4_bits_2_sobra[4], somador_4_bits_2_out_3}), .in1(somador_5_bits_2_out_3),
    .out(multiplexer_2_out), .sel(in_2[3]));  // open: en
  Multiplexer #(.width(5)) multiplexer_3 (
    .in0(multiplexer_1_out), .in1(multiplexer_2_out), .out(out_3), .sel(xnor_1_out));  // open: en
endmodule

module \Módulo  (
  input  [3:0] in_1,
  output [3:0] out_2
);

  wire [3:0] not_1_out, somador_4_bits_1_out_3;

  not not_1 (not_1_out[0], in_1[0]);
  not not_2 (not_1_out[1], in_1[1]);
  not not_3 (not_1_out[2], in_1[2]);
  not not_4 (not_1_out[3], in_1[3]);
  Somador_4_Bits somador_4_bits_1 (.in_1(not_1_out), .in_2(4'b0001), .out_3(somador_4_bits_1_out_3));  // open: SOBRA
  Multiplexer #(.width(4)) multiplexer_1 (
    .in0(in_1), .in1(somador_4_bits_1_out_3), .out(out_2), .sel(in_1[3]));  // open: en
endmodule

module Jogo_1 (
  input  [3:0] in_1,
  input  [3:0] in_2,
  input  [3:0] in_3,
  input  [3:0] in_4,
  output MENOR,
  output IGUAL,
  output MAIOR
);

  wire [4:0] n4_para_5_1_out_3, n4_para_5_2_out_3;

  _4_para_5 u_4_para_5_1 (.in_1(in_1), .in_2(in_2), .out_3(n4_para_5_1_out_3));
  _4_para_5 u_4_para_5_2 (.in_1(in_3), .in_2(in_4), .out_3(n4_para_5_2_out_3));
  comparador comparador_1 (
    .JGD(n4_para_5_1_out_3), .SCT(n4_para_5_2_out_3), .MENOR(MENOR), .ACERTOU(IGUAL), .MAIOR(MAIOR));
endmodule
